# Fritzing sketch Fritzing-Schematic (saved by Fritzing 0.9.2b)
breadboards: 1

parts:
  Part1 = Arduino Uno (Rev3)
  S1 = Pushbutton [package="[THT]"]
  R1 = Resistor [tolerance=±5% resistance=1k package=THT]
  LED1 = RGB LED (com. cathode, rgb) [package="5 mm [THT]"]
  R2 = Resistor [tolerance=±5% resistance=680 package=THT]
  J1 = Piezo Speaker
  Fingerprint_Scanner = mystery part, 4 pins [chip_label="Fingerprint Scanner"]
  R3 = Resistor [tolerance=±5% resistance=330 package=THT]
  R4 = Resistor [tolerance=±5% resistance=330 package=THT]
  R5 = Resistor [tolerance=±5% resistance=1k package=THT]
  Motion_Sensor = mystery part, 3 pins [chip_label="Motion Sensor"]

nets:
  N1: Part1.D8, LED1.red_anode
  N2: Part1.D9_PWM, J1.pin2
  N3: Part1.D10_PWM/SS, Motion_Sensor.pin1
  N4: Part1.D2, S1.Pin_1, S1.Pin_2, R1.Pin_0
  N5: Part1.D3_PWM, LED1.common_cathode
  N6: Part1.D4, Fingerprint_Scanner.pin1
  N7: Part1.D5_PWM, R3.Pin_1
  N8: Part1.5V, S1.Pin_3, S1.Pin_4, Fingerprint_Scanner.pin4, R5.Pin_0, Motion_Sensor.pin2
  N9: Part1.GND, R1.Pin_1, R2.Pin_1, J1.pin1, Fingerprint_Scanner.pin3, Motion_Sensor.pin3
  N10: LED1.blue_anode, R2.Pin_0
  N11: Fingerprint_Scanner.pin2, R4.Pin_0, R5.Pin_1
  N12: R3.Pin_0, R4.Pin_1
